// Logisim project pong_cpu.circ as structural Verilog
module FullAdder (
  input  A,
  input  B,
  input  Cin,
  output SUM,
  output COUT
);

  wire and_1_out, and_2_out, xor_1_out;

  xor xor_1 (xor_1_out, A, B);
  and and_1 (and_1_out, B, A);
  xor xor_2 (SUM, xor_1_out, Cin);
  and and_2 (and_2_out, Cin, xor_1_out);
  or or_1 (COUT, and_2_out, and_1_out);
endmodule

module FourBitAdder (
  input  A3,
  input  A2,
  input  A1,
  input  A0,
  input  B1,
  input  B2,
  input  B0,
  input  B3,
  input  C0,
  output COUT,
  output S3,
  output S2,
  output S1,
  output S0
);

  wire fulladder_2_cout, fulladder_3_cout, fulladder_4_cout;

  FullAdder fulladder_1 (.A(A3), .B(B3), .Cin(fulladder_2_cout), .SUM(S3), .COUT(COUT));
  FullAdder fulladder_2 (.A(A2), .B(B2), .Cin(fulladder_3_cout), .SUM(S2), .COUT(fulladder_2_cout));
  FullAdder fulladder_3 (.A(A1), .B(B1), .Cin(fulladder_4_cout), .SUM(S1), .COUT(fulladder_3_cout));
  FullAdder fulladder_4 (.A(A0), .B(B0), .Cin(C0), .SUM(S0), .COUT(fulladder_4_cout));
endmodule
